# Fritzing sketch scheme (saved by Fritzing 0.9.4)
breadboards: 1

parts:
  U1 = NodeMCU V3.0
  S1 = Pushbutton [package="[SMD]"]
  R1 = Resistor [tolerance=±5% resistance=220 package=THT]
  LED1 = smd LED [color="Red (633nm)" package="0805 [SMD]"]
  R2 = Resistor [tolerance=±5% resistance=220 package=THT]
  V1 = DC Power [voltage=5]

nets:
  N1: U1.D0, S1.Pin_3, S1.Pin_4, R1.Pin_0
  N2: U1.D2, R2.Pin_0
  N3: U1.3V3, S1.Pin_1, S1.Pin_2
  N4: U1.GND, R1.Pin_1, LED1.cathode, V1.V-
  N5: U1.Vin, V1.V+
  N6: LED1.anode, R2.Pin_1

custom parts:
  NodeMCU V3.0: ESP8266 based NodeMCU

// code stored in the sketch: NodemcuTemperatureRelayLcd.ino
#include <ESP8266HTTPClient.h>
#include <esp8266wifi.h>

const char* SSID         = "wifi_ssid";
const char* PASSWORD     = "wifi_password";
const char* HTTP_URL     = "http://ip.to.server/change-event";
const int   TIME_TO_WAIT = 1000;

int  PUSH_BUTTON = 16;
int  LED         = 4;
long pressMoment;

void setup() {
  Serial.begin(9600);
  
  pinMode(LED, OUTPUT);
  pinMode(PUSH_BUTTON, INPUT);
  
  pressMoment = millis();
  digitalWrite(LED, LOW);

  WiFi.begin(SSID, PASSWORD);
  while (WiFi.status() != WL_CONNECTED) { 
    Serial.println("Connecting...");
    delay(1000);  
  }
  Serial.println("Connected!");
}

void loop() {    
  int buttonValue = digitalRead(PUSH_BUTTON);

  if (buttonValue == HIGH && waitedTime(pressMoment)) {
    Serial.println("Pushed");
    httpRequest();
    pressMoment = millis();
  }
}

void httpRequest () {
    digitalWrite(LED, HIGH);
    
    if (WiFi.status() == WL_CONNECTED) {
      
      HTTPClient http;
      http.begin(HTTP_URL);
      http.addHeader("Content-Type", "text/plain");
      
      int httpCode = http.POST("");

      if (httpCode == 200) {
        String payload = http.getString();
        Serial.println(payload);  
      } else {
        Serial.println("Bad request");
      }
    } else {
      Serial.println("Wifi not connected");
    }

    digitalWrite(LED, LOW);  
}

boolean waitedTime(long pressMoment) {
  return (millis() - pressMoment) > TIME_TO_WAIT; 
}
